// Digital circuit New_Address_Decode.dig as structural Verilog
module New_Address_Decode (
  input  A0,
  input  A1,
  input  A2,
  input  A3,
  input  A4,
  input  A5,
  input  A6,
  input  A7,
  input  A8,
  input  A9,
  input  A10,
  input  A11,
  input  A12,
  input  R_nW,
  input  AS,
  output RAM_2_nCE,
  output nQ4,
  output nQ5,
  output nQ6,
  output nQ7,
  output ROM_nCE,
  output out_22,
  output out_23,
  output out_24,
  output out_25,
  output out_26,
  output out_27,
  output out_28,
  output out_29
);

  wire MX1_pin12, MX1_pin13, MX1_pin15;

  _74138 MX1 (
    .pin1(A11), .pin2(A12), .pin3(1'b0), .pin4(1'b0), .pin5(1'b0), .pin6(AS), .pin7(nQ7), .pin8(1'b0),
    .pin9(nQ6), .pin10(nQ5), .pin11(nQ4), .pin12(MX1_pin12), .pin13(MX1_pin13), .pin14(RAM_2_nCE),
    .pin15(MX1_pin15), .pin16(1'b1));
  _74138 MX2 (
    .pin1(A8), .pin2(A9), .pin3(A10), .pin4(MX1_pin15), .pin5(MX1_pin15), .pin6(AS), .pin7(out_29),
    .pin8(1'b0), .pin9(out_28), .pin10(out_27), .pin11(out_26), .pin12(out_25), .pin13(out_24),
    .pin14(out_23), .pin15(out_22), .pin16(1'b1));
  and and_1 (ROM_nCE, MX1_pin13, MX1_pin12);

  // Notes on the sheet:
  //   R_nW: Read High, Write Low
  //   AS: Address Select
  //   RAM_2_nCE: RAM 2 ~CE
endmodule
